# Fritzing sketch bme280_schema (saved by Fritzing 0.9.4)
breadboards: 1

parts:
  U2 = NodeMCU V1.0
  M1 = BME280

nets:
  3V3: U2.3V3, M1.VIN
  GND: U2.GND, M1.GND
  N1: U2.D5, M1.SCL
  N2: U2.D6, M1.SDA

custom parts:
  NodeMCU V1.0: ESP8266 based NodeMCU
  BME280: Temperature Humidity Barometric presure Sensor
