# Fritzing sketch tsl2591_schema (saved by Fritzing 0.9.4)
breadboards: 1

parts:
  Part1 = Adafruit TSL2591 High Dynamic Range Digital Light Sensor [part_number="Adafruit #1980"]
  U2 = NodeMCU V1.0

nets:
  GND: Part1.GND, U2.GND
  N1: Part1.SCL, U2.D1
  VCC: Part1.VCC, U2.3V3
  N2: Part1.SDA, U2.D2

custom parts:
  Adafruit TSL2591 High Dynamic Range Digital Light Sensor: When the future is dazzlingly-bright, this ultra-high-range luminosity sensor will help you measure it. The TSL2591 luminosity sensor is an advanced digital light sensor, ideal for use in a wide range of light situations. Compared to low cost CdS cells, this sensor is more precise, allowing for exact lux calculations and can be configured for different gain/timing ranges to detect light ranges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
  NodeMCU V1.0: ESP8266 based NodeMCU
